// Logisim project Simulation Simplified.circ as structural Verilog: 1 circuit, main circuit main
// true
module main (
);

  wire _0_2_out, _0_out, _1_2_out, _1_out, _2_2_out, _2_out, _3_2_out, _3_out, _4_2_out, _4_out, _5_2_out,
       _5_out, _6_2_out, _6_out, _7_2_out, _7_out, _8_2_out, _8_out, _9_2_out, _9_out, A_2_out, A_out,
       and_1_out, and_2_out, and_3_out, and_4_out, and_5_out, and_6_out, and_7_out, and_8_out, and_9_out,
       and_10_out, and_11_out, and_12_out, and_13_out, and_14_out, and_15_out, and_16_out, and_17_out,
       and_18_out, and_19_out, B_2_out, B_out, button_2_out, button_out, C_2_out, C_out, Checker_2_out,
       Checker_3_out, Checker_out, Clock_out, D_2_out, d_ff_1_q, d_ff_2_q, d_ff_3_q, d_ff_4_q, d_ff_5_q,
       d_ff_6_q, d_ff_7_q, d_ff_8_q, d_ff_9_q, d_ff_10_q, d_ff_11_q, d_ff_12_q, d_ff_13_q, d_ff_14_q,
       d_ff_15_q, d_ff_16_q, d_ff_17_q, d_ff_18_q, d_ff_19_q, d_ff_20_q, d_ff_21_q, d_ff_22_q, d_ff_23_q,
       d_ff_24_q, d_ff_25_q, d_ff_26_q, d_ff_27_q, d_ff_28_q, d_ff_29_q, d_ff_30_q, d_ff_31_q, d_ff_32_q,
       D_out, Mode_Toggler_q, Mode_Toggler_qn, n7_segment_display_driver_1_p5,
       n7_segment_display_driver_1_p6, n7_segment_display_driver_1_p7, n7_segment_display_driver_1_p8,
       n7_segment_display_driver_1_p9, n7_segment_display_driver_1_p10, n7_segment_display_driver_1_p11,
       n7_segment_display_driver_2_p5, n7_segment_display_driver_2_p6, n7_segment_display_driver_2_p7,
       n7_segment_display_driver_2_p8, n7_segment_display_driver_2_p9, n7_segment_display_driver_2_p10,
       n7_segment_display_driver_2_p11, n7_segment_display_driver_3_p5, n7_segment_display_driver_3_p6,
       n7_segment_display_driver_3_p7, n7_segment_display_driver_3_p8, n7_segment_display_driver_3_p9,
       n7_segment_display_driver_3_p10, n7_segment_display_driver_3_p11, n7_segment_display_driver_4_p5,
       n7_segment_display_driver_4_p6, n7_segment_display_driver_4_p7, n7_segment_display_driver_4_p8,
       n7_segment_display_driver_4_p9, n7_segment_display_driver_4_p10, n7_segment_display_driver_4_p11,
       n7_segment_display_driver_5_p5, n7_segment_display_driver_5_p6, n7_segment_display_driver_5_p7,
       n7_segment_display_driver_5_p8, n7_segment_display_driver_5_p9, n7_segment_display_driver_5_p10,
       n7_segment_display_driver_5_p11, n7_segment_display_driver_6_p5, n7_segment_display_driver_6_p6,
       n7_segment_display_driver_6_p7, n7_segment_display_driver_6_p8, n7_segment_display_driver_6_p9,
       n7_segment_display_driver_6_p10, n7_segment_display_driver_6_p11, n7_segment_display_driver_7_p5,
       n7_segment_display_driver_7_p6, n7_segment_display_driver_7_p7, n7_segment_display_driver_7_p8,
       n7_segment_display_driver_7_p9, n7_segment_display_driver_7_p10, n7_segment_display_driver_7_p11,
       n7_segment_display_driver_8_p5, n7_segment_display_driver_8_p6, n7_segment_display_driver_8_p7,
       n7_segment_display_driver_8_p8, n7_segment_display_driver_8_p9, n7_segment_display_driver_8_p10,
       n7_segment_display_driver_8_p11, nor_1_out, or_1_out, Pin_1_out, Pin_2_out, Pin_3_out, Pin_4_out,
       Pin_5_out, Pin_6_out, Pin_7_out, Pin_8_out, priority_encoder_1_gs, T0_2_q, T0_q, T1_2_q, T1_q,
       xor_1_out, xor_2_out, xor_3_out, xor_4_out, xor_5_out, xor_6_out, xor_7_out, xor_8_out, xor_9_out,
       xor_10_out, xor_11_out, xor_12_out, xor_13_out, xor_14_out, xor_15_out, xor_16_out;
  wire [3:0] priority_encoder_1_out;

  Button _1 (.out(_1_out));
  Button _4 (.out(_4_out));
  Button _7 (.out(_7_out));
  Button button (.out(button_out));
  or Pin_5 (Pin_5_out, button_out, _7_out, _4_out, _1_out);
  Button _2 (.out(_2_out));
  Button _5 (.out(_5_out));
  Button _8 (.out(_8_out));
  Button _0 (.out(_0_out));
  or Pin_6 (Pin_6_out, _0_out, _8_out, _5_out, _2_out);
  Button _3 (.out(_3_out));
  Button _6 (.out(_6_out));
  Button _9 (.out(_9_out));
  Button button_2 (.out(button_2_out));
  or Pin_7 (Pin_7_out, button_2_out, _9_out, _6_out, _3_out);
  Button A (.out(A_out));
  Button B (.out(B_out));
  Button C (.out(C_out));
  Button D (.out(D_out));
  or Pin_8 (Pin_8_out, D_out, C_out, B_out, A_out);
  or Pin_1 (Pin_1_out, _1_out, _2_out, _3_out, A_out);
  or Pin_2 (Pin_2_out, _4_out, _5_out, _6_out, B_out);
  or Pin_3 (Pin_3_out, _7_out, _8_out, _9_out, C_out);
  or Pin_4 (Pin_4_out, button_out, _0_out, button_2_out, D_out);
  and and_1 (and_1_out, ~Pin_4_out, Pin_5_out);  // AND_Gate
  and and_2 (and_2_out, ~Pin_4_out, Pin_7_out);  // AND_Gate
  and _1_2 (_1_2_out, Pin_1_out, Pin_5_out);
  and _2_2 (_2_2_out, Pin_1_out, Pin_6_out);
  and _3_2 (_3_2_out, Pin_1_out, Pin_7_out);
  and A_2 (A_2_out, Pin_1_out, Pin_8_out);
  and _4_2 (_4_2_out, Pin_2_out, Pin_5_out);
  and _5_2 (_5_2_out, Pin_2_out, Pin_6_out);
  and _6_2 (_6_2_out, Pin_2_out, Pin_7_out);
  and B_2 (B_2_out, Pin_2_out, Pin_8_out);
  and _7_2 (_7_2_out, Pin_3_out, Pin_5_out);
  and _8_2 (_8_2_out, Pin_3_out, Pin_6_out);
  and _9_2 (_9_2_out, Pin_3_out, Pin_7_out);
  and C_2 (C_2_out, Pin_3_out, Pin_8_out);
  and and_3 (and_3_out, Pin_4_out, Pin_5_out);
  and _0_2 (_0_2_out, Pin_4_out, Pin_6_out);
  and and_4 (and_4_out, Pin_4_out, Pin_7_out);
  and D_2 (D_2_out, Pin_4_out, Pin_8_out);
  Priority_Encoder #(.select(4), .disabled(0)) priority_encoder_1 (
    .in0(_0_2_out), .in1(_1_2_out), .in2(_2_2_out), .in3(_3_2_out), .in4(_4_2_out), .in5(_5_2_out),
    .in6(_6_2_out), .in7(_7_2_out), .in8(_8_2_out), .in9(_9_2_out), .in10(A_2_out), .in11(B_2_out),
    .in12(C_2_out), .in13(D_2_out), .in14(and_3_out), .in15(and_4_out), .out(priority_encoder_1_out),
    .gs(priority_encoder_1_gs));  // open: en_out, en_in
  or Clock (Clock_out, Pin_8_out, and_2_out, Pin_6_out, and_1_out);
  and and_5 (and_5_out, priority_encoder_1_gs, priority_encoder_1_out[3]);
  and and_6 (and_6_out, priority_encoder_1_gs, priority_encoder_1_out[2]);
  and and_7 (and_7_out, priority_encoder_1_out[1], priority_encoder_1_gs);
  and and_8 (and_8_out, priority_encoder_1_out[0], priority_encoder_1_gs);
  or or_1 (or_1_out, and_9_out, Mode_Toggler_qn);
  and and_9 (and_9_out, nor_1_out, Mode_Toggler_q);
  and and_10 (and_10_out, Mode_Toggler_q, Clock_out);
  and and_11 (and_11_out, Mode_Toggler_qn, Clock_out);
  and Checker (Checker_out, or_1_out, and_8_out, and_7_out, and_6_out, and_5_out);
  and Checker_2 (Checker_2_out, Mode_Toggler_q, and_5_out, and_6_out, and_7_out, ~and_8_out);  // AND_Gate
  and Checker_3 (Checker_3_out, Mode_Toggler_qn, and_5_out, and_6_out, and_7_out, ~and_8_out);  // AND_Gate
  T_Flip_Flop Mode_Toggler (
    .clk(Checker_out), .T(1'b1), .Q(Mode_Toggler_q), .Qn(Mode_Toggler_qn));  // open: preset, reset, en
  and and_12 (and_12_out, ~T1_q, ~T0_q);  // AND_Gate
  and and_13 (and_13_out, ~T1_q, T0_q);  // AND_Gate
  and and_14 (and_14_out, T1_q, ~T0_q);  // AND_Gate
  and and_15 (and_15_out, T1_q, T0_q);
  and and_16 (and_16_out, ~T1_2_q, ~T0_2_q);  // AND_Gate
  and and_17 (and_17_out, ~T1_2_q, T0_2_q);  // AND_Gate
  and and_18 (and_18_out, T1_2_q, ~T0_2_q);  // AND_Gate
  and and_19 (and_19_out, T1_2_q, T0_2_q);
  D_Flip_Flop d_ff_1 (
    .clk(and_12_out), .D(and_5_out), .Q(d_ff_1_q), .en(and_12_out), .reset(Checker_2_out));  // open: Qn, preset
  D_Flip_Flop d_ff_2 (
    .clk(and_13_out), .D(and_5_out), .Q(d_ff_2_q), .en(and_13_out), .reset(Checker_2_out));  // open: Qn, preset
  D_Flip_Flop d_ff_3 (
    .clk(and_14_out), .D(and_5_out), .Q(d_ff_3_q), .en(and_14_out), .reset(Checker_2_out));  // open: Qn, preset
  D_Flip_Flop d_ff_4 (
    .clk(and_15_out), .D(and_5_out), .Q(d_ff_4_q), .en(and_15_out), .reset(Checker_2_out));  // open: Qn, preset
  D_Flip_Flop d_ff_5 (
    .clk(and_16_out), .D(and_5_out), .Q(d_ff_5_q), .en(and_16_out), .reset(Checker_3_out));  // open: Qn, preset
  D_Flip_Flop d_ff_6 (
    .clk(and_17_out), .D(and_5_out), .Q(d_ff_6_q), .en(and_17_out), .reset(Checker_3_out));  // open: Qn, preset
  D_Flip_Flop d_ff_7 (
    .clk(and_18_out), .D(and_5_out), .Q(d_ff_7_q), .en(and_18_out), .reset(Checker_3_out));  // open: Qn, preset
  D_Flip_Flop d_ff_8 (
    .clk(and_19_out), .D(and_5_out), .Q(d_ff_8_q), .en(and_19_out), .reset(Checker_3_out));  // open: Qn, preset
  T_Flip_Flop T1 (.clk(and_10_out), .T(T0_q), .Q(T1_q), .preset(Checker_2_out));  // open: Qn, reset, en
  D_Flip_Flop d_ff_9 (
    .clk(and_12_out), .D(and_6_out), .Q(d_ff_9_q), .en(and_12_out), .reset(Checker_2_out));  // open: Qn, preset
  D_Flip_Flop d_ff_10 (
    .clk(and_13_out), .D(and_6_out), .Q(d_ff_10_q), .en(and_13_out), .reset(Checker_2_out));  // open: Qn, preset
  D_Flip_Flop d_ff_11 (
    .clk(and_14_out), .D(and_6_out), .Q(d_ff_11_q), .en(and_14_out), .reset(Checker_2_out));  // open: Qn, preset
  D_Flip_Flop d_ff_12 (
    .clk(and_15_out), .D(and_6_out), .Q(d_ff_12_q), .en(and_15_out), .reset(Checker_2_out));  // open: Qn, preset
  T_Flip_Flop T1_2 (.clk(and_11_out), .T(T0_2_q), .Q(T1_2_q), .preset(Checker_3_out));  // open: Qn, reset, en
  D_Flip_Flop d_ff_13 (
    .clk(and_16_out), .D(and_6_out), .Q(d_ff_13_q), .en(and_16_out), .reset(Checker_3_out));  // open: Qn, preset
  D_Flip_Flop d_ff_14 (
    .clk(and_17_out), .D(and_6_out), .Q(d_ff_14_q), .en(and_17_out), .reset(Checker_3_out));  // open: Qn, preset
  D_Flip_Flop d_ff_15 (
    .clk(and_18_out), .D(and_6_out), .Q(d_ff_15_q), .en(and_18_out), .reset(Checker_3_out));  // open: Qn, preset
  D_Flip_Flop d_ff_16 (
    .clk(and_19_out), .D(and_6_out), .Q(d_ff_16_q), .en(and_19_out), .reset(Checker_3_out));  // open: Qn, preset
  T_Flip_Flop T0 (.clk(and_10_out), .T(1'b1), .Q(T0_q), .preset(Checker_2_out));  // open: Qn, reset, en
  D_Flip_Flop d_ff_17 (
    .clk(and_12_out), .D(and_7_out), .Q(d_ff_17_q), .en(and_12_out), .reset(Checker_2_out));  // open: Qn, preset
  D_Flip_Flop d_ff_18 (
    .clk(and_13_out), .D(and_7_out), .Q(d_ff_18_q), .en(and_13_out), .reset(Checker_2_out));  // open: Qn, preset
  D_Flip_Flop d_ff_19 (
    .clk(and_14_out), .D(and_7_out), .Q(d_ff_19_q), .en(and_14_out), .reset(Checker_2_out));  // open: Qn, preset
  D_Flip_Flop d_ff_20 (
    .clk(and_15_out), .D(and_7_out), .Q(d_ff_20_q), .en(and_15_out), .reset(Checker_2_out));  // open: Qn, preset
  T_Flip_Flop T0_2 (.clk(and_11_out), .T(1'b1), .Q(T0_2_q), .preset(Checker_3_out));  // open: Qn, reset, en
  D_Flip_Flop d_ff_21 (
    .clk(and_16_out), .D(and_7_out), .Q(d_ff_21_q), .en(and_16_out), .reset(Checker_3_out));  // open: Qn, preset
  D_Flip_Flop d_ff_22 (
    .clk(and_17_out), .D(and_7_out), .Q(d_ff_22_q), .en(and_17_out), .reset(Checker_3_out));  // open: Qn, preset
  D_Flip_Flop d_ff_23 (
    .clk(and_18_out), .D(and_7_out), .Q(d_ff_23_q), .en(and_18_out), .reset(Checker_3_out));  // open: Qn, preset
  D_Flip_Flop d_ff_24 (
    .clk(and_19_out), .D(and_7_out), .Q(d_ff_24_q), .en(and_19_out), .reset(Checker_3_out));  // open: Qn, preset
  D_Flip_Flop d_ff_25 (
    .clk(and_12_out), .D(and_8_out), .Q(d_ff_25_q), .en(and_12_out), .reset(Checker_2_out));  // open: Qn, preset
  D_Flip_Flop d_ff_26 (
    .clk(and_13_out), .D(and_8_out), .Q(d_ff_26_q), .en(and_13_out), .reset(Checker_2_out));  // open: Qn, preset
  D_Flip_Flop d_ff_27 (
    .clk(and_14_out), .D(and_8_out), .Q(d_ff_27_q), .en(and_14_out), .reset(Checker_2_out));  // open: Qn, preset
  D_Flip_Flop d_ff_28 (
    .clk(and_15_out), .D(and_8_out), .Q(d_ff_28_q), .en(and_15_out), .reset(Checker_2_out));  // open: Qn, preset
  D_Flip_Flop d_ff_29 (
    .clk(and_16_out), .D(and_8_out), .Q(d_ff_29_q), .en(and_16_out), .reset(Checker_3_out));  // open: Qn, preset
  D_Flip_Flop d_ff_30 (
    .clk(and_17_out), .D(and_8_out), .Q(d_ff_30_q), .en(and_17_out), .reset(Checker_3_out));  // open: Qn, preset
  D_Flip_Flop d_ff_31 (
    .clk(and_18_out), .D(and_8_out), .Q(d_ff_31_q), .en(and_18_out), .reset(Checker_3_out));  // open: Qn, preset
  D_Flip_Flop d_ff_32 (
    .clk(and_19_out), .D(and_8_out), .Q(d_ff_32_q), .en(and_19_out), .reset(Checker_3_out));  // open: Qn, preset
  // _7_segment_display_driver 7_segment_display_driver_1: pin names not known; wires that end beside it: d_ff_1_q, d_ff_9_q, d_ff_17_q, d_ff_25_q, n7_segment_display_driver_1_p5, n7_segment_display_driver_1_p6, n7_segment_display_driver_1_p7, n7_segment_display_driver_1_p8, n7_segment_display_driver_1_p9, n7_segment_display_driver_1_p10, n7_segment_display_driver_1_p11
  // _7_segment_display_driver 7_segment_display_driver_2: pin names not known; wires that end beside it: d_ff_2_q, d_ff_10_q, d_ff_18_q, d_ff_26_q, n7_segment_display_driver_2_p5, n7_segment_display_driver_2_p6, n7_segment_display_driver_2_p7, n7_segment_display_driver_2_p8, n7_segment_display_driver_2_p9, n7_segment_display_driver_2_p10, n7_segment_display_driver_2_p11
  // _7_segment_display_driver 7_segment_display_driver_3: pin names not known; wires that end beside it: d_ff_3_q, d_ff_11_q, d_ff_19_q, d_ff_27_q, n7_segment_display_driver_3_p5, n7_segment_display_driver_3_p6, n7_segment_display_driver_3_p7, n7_segment_display_driver_3_p8, n7_segment_display_driver_3_p9, n7_segment_display_driver_3_p10, n7_segment_display_driver_3_p11
  // _7_segment_display_driver 7_segment_display_driver_4: pin names not known; wires that end beside it: d_ff_4_q, d_ff_12_q, d_ff_20_q, d_ff_28_q, n7_segment_display_driver_4_p5, n7_segment_display_driver_4_p6, n7_segment_display_driver_4_p7, n7_segment_display_driver_4_p8, n7_segment_display_driver_4_p9, n7_segment_display_driver_4_p10, n7_segment_display_driver_4_p11
  // _7_segment_display_driver 7_segment_display_driver_5: pin names not known; wires that end beside it: d_ff_5_q, d_ff_13_q, d_ff_21_q, d_ff_29_q, n7_segment_display_driver_5_p5, n7_segment_display_driver_5_p6, n7_segment_display_driver_5_p7, n7_segment_display_driver_5_p8, n7_segment_display_driver_5_p9, n7_segment_display_driver_5_p10, n7_segment_display_driver_5_p11
  // _7_segment_display_driver 7_segment_display_driver_6: pin names not known; wires that end beside it: d_ff_6_q, d_ff_14_q, d_ff_22_q, d_ff_30_q, n7_segment_display_driver_6_p5, n7_segment_display_driver_6_p6, n7_segment_display_driver_6_p7, n7_segment_display_driver_6_p8, n7_segment_display_driver_6_p9, n7_segment_display_driver_6_p10, n7_segment_display_driver_6_p11
  // _7_segment_display_driver 7_segment_display_driver_7: pin names not known; wires that end beside it: d_ff_7_q, d_ff_15_q, d_ff_23_q, d_ff_31_q, n7_segment_display_driver_7_p5, n7_segment_display_driver_7_p6, n7_segment_display_driver_7_p7, n7_segment_display_driver_7_p8, n7_segment_display_driver_7_p9, n7_segment_display_driver_7_p10, n7_segment_display_driver_7_p11
  // _7_segment_display_driver 7_segment_display_driver_8: pin names not known; wires that end beside it: d_ff_8_q, d_ff_16_q, d_ff_24_q, d_ff_32_q, n7_segment_display_driver_8_p5, n7_segment_display_driver_8_p6, n7_segment_display_driver_8_p7, n7_segment_display_driver_8_p8, n7_segment_display_driver_8_p9, n7_segment_display_driver_8_p10, n7_segment_display_driver_8_p11
  _7_Segment_Display u_7_segment_display_1 (
    .g(n7_segment_display_driver_1_p11), .f(n7_segment_display_driver_1_p10),
    .a(n7_segment_display_driver_1_p5), .b(n7_segment_display_driver_1_p6),
    .e(n7_segment_display_driver_1_p9), .d(n7_segment_display_driver_1_p8), .c(n7_segment_display_driver_1_p7));  // open: dp
  _7_Segment_Display u_7_segment_display_2 (
    .g(n7_segment_display_driver_2_p11), .f(n7_segment_display_driver_2_p10),
    .a(n7_segment_display_driver_2_p5), .b(n7_segment_display_driver_2_p6),
    .e(n7_segment_display_driver_2_p9), .d(n7_segment_display_driver_2_p8), .c(n7_segment_display_driver_2_p7));  // open: dp
  _7_Segment_Display u_7_segment_display_3 (
    .g(n7_segment_display_driver_3_p11), .f(n7_segment_display_driver_3_p10),
    .a(n7_segment_display_driver_3_p5), .b(n7_segment_display_driver_3_p6),
    .e(n7_segment_display_driver_3_p9), .d(n7_segment_display_driver_3_p8), .c(n7_segment_display_driver_3_p7));  // open: dp
  _7_Segment_Display u_7_segment_display_4 (
    .g(n7_segment_display_driver_4_p11), .f(n7_segment_display_driver_4_p10),
    .a(n7_segment_display_driver_4_p5), .b(n7_segment_display_driver_4_p6),
    .e(n7_segment_display_driver_4_p9), .d(n7_segment_display_driver_4_p8), .c(n7_segment_display_driver_4_p7));  // open: dp
  _7_Segment_Display u_7_segment_display_5 (
    .g(n7_segment_display_driver_5_p11), .f(n7_segment_display_driver_5_p10),
    .a(n7_segment_display_driver_5_p5), .b(n7_segment_display_driver_5_p6),
    .e(n7_segment_display_driver_5_p9), .d(n7_segment_display_driver_5_p8), .c(n7_segment_display_driver_5_p7));  // open: dp
  _7_Segment_Display u_7_segment_display_6 (
    .g(n7_segment_display_driver_6_p11), .f(n7_segment_display_driver_6_p10),
    .a(n7_segment_display_driver_6_p5), .b(n7_segment_display_driver_6_p6),
    .e(n7_segment_display_driver_6_p9), .d(n7_segment_display_driver_6_p8), .c(n7_segment_display_driver_6_p7));  // open: dp
  _7_Segment_Display u_7_segment_display_7 (
    .g(n7_segment_display_driver_7_p11), .f(n7_segment_display_driver_7_p10),
    .a(n7_segment_display_driver_7_p5), .b(n7_segment_display_driver_7_p6),
    .e(n7_segment_display_driver_7_p9), .d(n7_segment_display_driver_7_p8), .c(n7_segment_display_driver_7_p7));  // open: dp
  _7_Segment_Display u_7_segment_display_8 (
    .g(n7_segment_display_driver_8_p11), .f(n7_segment_display_driver_8_p10),
    .a(n7_segment_display_driver_8_p5), .b(n7_segment_display_driver_8_p6),
    .e(n7_segment_display_driver_8_p9), .d(n7_segment_display_driver_8_p8), .c(n7_segment_display_driver_8_p7));  // open: dp
  xor xor_1 (xor_1_out, d_ff_1_q, d_ff_5_q);
  xor xor_2 (xor_2_out, d_ff_9_q, d_ff_13_q);
  xor xor_3 (xor_3_out, d_ff_17_q, d_ff_21_q);
  xor xor_4 (xor_4_out, d_ff_25_q, d_ff_29_q);
  xor xor_5 (xor_5_out, d_ff_2_q, d_ff_6_q);
  xor xor_6 (xor_6_out, d_ff_10_q, d_ff_14_q);
  xor xor_7 (xor_7_out, d_ff_18_q, d_ff_22_q);
  xor xor_8 (xor_8_out, d_ff_26_q, d_ff_30_q);
  xor xor_9 (xor_9_out, d_ff_3_q, d_ff_7_q);
  xor xor_10 (xor_10_out, d_ff_11_q, d_ff_15_q);
  xor xor_11 (xor_11_out, d_ff_19_q, d_ff_23_q);
  xor xor_12 (xor_12_out, d_ff_27_q, d_ff_31_q);
  xor xor_13 (xor_13_out, d_ff_4_q, d_ff_8_q);
  xor xor_14 (xor_14_out, d_ff_12_q, d_ff_16_q);
  xor xor_15 (xor_15_out, d_ff_20_q, d_ff_24_q);
  xor xor_16 (xor_16_out, d_ff_28_q, d_ff_32_q);
  nor nor_1 (nor_1_out, xor_1_out, xor_2_out, xor_3_out, xor_4_out, xor_5_out, xor_6_out, xor_7_out, xor_8_out, xor_9_out, xor_10_out, xor_11_out, xor_12_out, xor_13_out, xor_14_out, xor_15_out, xor_16_out);
  LED led_1 (.in(nor_1_out));

  // Notes on the sheet:
  //   0 means Reg Mode
  //   1 means Authentication Mode
endmodule
